# Fritzing sketch design (saved by Fritzing 0.9.3b)

parts:
  Part1 = Adafruit Stereo 2.1W Class D Audio Amplifier - TPA2012 [part_number="Adafruit #1552"]
  SP1 = SPEAKER [package=pcb_mount_speaker]
  SP2 = SPEAKER [package=pcb_mount_speaker]
  Raspberry_Pi_1 = Raspberry Pi 3 [part_number=RPI-3-V1.2]  # not connected
  Part2 = Arduino Uno (Rev3)
  JOY1 = Adafruit Arcade Joystick
  BUTTON1 = Arcade Button (red)
  BUTTON2 = Arcade Button (red)
  BUTTON3 = Arcade Button (red)
  BUTTON4 = Arcade Button (red)
  BUTTON5 = Arcade Button (red)
  BUTTON6 = Arcade Button (red)
  Part3 = Arduino Uno (Rev3)
  JOY2 = Adafruit Arcade Joystick
  BUTTON7 = Arcade Button (red)
  BUTTON8 = Arcade Button (red)
  BUTTON9 = Arcade Button (red)
  BUTTON10 = Arcade Button (red)
  BAT1 = BC9VPC [package=bc9vpc]

nets:
  N1: Part1.VDD, BAT1.V+
  N2: Part1.GND, BAT1.V-
  N3: Part1.IN_RIGHT+, SP1.-
  N4: Part1.IN_RIGHT-, SP1.+
  N5: Part1.IN_LEFT-, SP2.+
  N6: Part1.IN_LEFT+, SP2.-
  N7: Part2.A4/SDA, BUTTON6.no_name_yet#2
  N8: Part2.D8, JOY1.W
  N9: Part2.D9_PWM, JOY1.E
  N10: Part2.D12/MISO, BUTTON5.no_name_yet#2
  N11: Part2.GND, JOY1.COM, BUTTON1.no_name_yet#1, BUTTON2.no_name_yet#1, BUTTON3.no_name_yet#1, BUTTON4.no_name_yet#1, BUTTON5.no_name_yet#1, BUTTON6.no_name_yet#1
  N12: Part2.D2, BUTTON1.no_name_yet#2
  N13: Part2.D3_PWM, BUTTON2.no_name_yet#2
  N14: Part2.D4, BUTTON3.no_name_yet#2
  N15: Part2.D5_PWM, BUTTON4.no_name_yet#2
  N16: Part2.D6_PWM, JOY1.N
  N17: Part2.D7, JOY1.S
  N18: Part3.D8, JOY2.W
  N19: Part3.D9_PWM, JOY2.E
  N20: Part3.GND, JOY2.COM, BUTTON7.no_name_yet#1, BUTTON8.no_name_yet#1, BUTTON9.no_name_yet#1, BUTTON10.no_name_yet#1
  N21: Part3.D2, BUTTON7.no_name_yet#2
  N22: Part3.D3_PWM, BUTTON8.no_name_yet#2
  N23: Part3.D4, BUTTON9.no_name_yet#2
  N24: Part3.D5_PWM, BUTTON10.no_name_yet#2
  N25: Part3.D6_PWM, JOY2.N
  N26: Part3.D7, JOY2.S

custom parts:
  Adafruit Stereo 2.1W Class D Audio Amplifier - TPA2012: This incredibly small stereo amplifier is surprisingly powerful - able to deliver 2 x 2.1W channels into 4 ohm impedance speakers (@ 10% THD). Inside the miniature chip is a class D controller, able to run from 2.7V-5.5VDC. Since the amp is a class D, it's incredibly efficient (89% efficient when driving an 8Ω speaker at 1.5 Watt) - making it perfect for portable and battery-powered projects.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
  Arcade Button (red): Adafruit Arcade Button (red)
